// Logisim project lab_2_ex_10.circ as structural Verilog: 1 circuit, main circuit main
module main (
  input  D,
  input  CLK
);

  wire d_ff_1_q;

  D_Flip_Flop d_ff_1 (.clk(D), .D(CLK), .Q(d_ff_1_q));  // open: Qn, preset, en, reset
  // Probe on nothing
endmodule
